// Logisim project TicTacToe(1) (2).circ as structural Verilog
module main (
);

  wire and_3_out, and_4_out, and_5_out, button_1_out, button_2_out, button_3_out, button_4_out, button_5_out,
       button_6_out, button_7_out, button_8_out, button_9_out, cdm_8_mark5_1_p1, cdm_8_mark5_1_p2,
       cdm_8_mark5_1_p4, cdm_8_mark5_1_p5, cdm_8_mark5_1_p6, cdm_8_mark5_1_p7, cdm_8_mark5_1_p8,
       cdm_8_mark5_1_p9, Cl, code, comparator_1_gt, comparator_2_eq, data, decoder_1_out0, decoder_1_out1,
       I_Osel, i_win_1_draw, i_win_1_lose, i_win_1_win, In_out_prime, IO_3_2_out, IO_3_3_out, IO_3_out, mem,
       not_1_out, RAM, rst;
  wire [1:0] _00, _01, _02, _10, _11, _12, _20, _21, _22, lll1_1_h0, lll1_1_h1, lll1_1_h2, lll1_1_v0,
       lll1_1_v1, lll1_1_v2, State;
  wire [2:2] tttc_1_hout, tttc_1_vout, tttc_2_hout, tttc_3_hout, tttc_4_vout, tttc_7_vout;
  wire [3:0] cdm_8_mark5_1_p12, I_Oadr, tttc_1_l0, tttc_1_l1, tttc_1_l2, tttc_1_l3, tttc_2_l0, tttc_2_l1,
       tttc_2_l2, tttc_2_l3, tttc_3_l0, tttc_3_l1, tttc_3_l2, tttc_3_l3, tttc_4_l0, tttc_4_l1, tttc_4_l2,
       tttc_4_l3, tttc_5_l0, tttc_5_l1, tttc_5_l2, tttc_5_l3, tttc_6_l0, tttc_6_l1, tttc_6_l2, tttc_6_l3,
       tttc_7_l0, tttc_7_l1, tttc_7_l2, tttc_7_l3, tttc_8_l0, tttc_8_l1, tttc_8_l2, tttc_8_l3, tttc_9_l0,
       tttc_9_l1, tttc_9_l2, tttc_9_l3;
  wire [7:0] bbb_1_xy, cdm_8_mark5_1_p13, cdm_8_mark5_1_p14, comp_turn_1_nought_coord, I_Odat;

  LED led_1 (.in(i_win_1_win));
  LED led_2 (.in(i_win_1_lose));
  // Probe on I_Odat[5:2]
  // Probe on I_Oadr
  // Probe on I_Odat
  LED led_3 (.in(i_win_1_draw));
  I_Win i_win_1 (
    .score(I_Odat[7:6]), .clock(decoder_1_out0), .lose(i_win_1_lose), .win(i_win_1_win), .draw(i_win_1_draw));
  LLL1 lll1_1 (
    .symID(I_Odat[1:0]), .XY(I_Odat[5:2]), .clock(decoder_1_out0), .V0(lll1_1_v0), .V1(lll1_1_v1),
    .V2(lll1_1_v2), .H0(lll1_1_h0), .H1(lll1_1_h1), .H2(lll1_1_h2));
  and IO_3 (IO_3_out, I_Osel, ~I_Oadr[0], ~I_Oadr[1], ~I_Oadr[2], ~I_Oadr[3]);  // AND_Gate
  Decoder #(.disabled(0)) decoder_1 (.out0(decoder_1_out0), .out1(decoder_1_out1), .sel(In_out_prime), .en(IO_3_out));
  DotMatrix #(.inputtype("row"), .matrixcols(4), .matrixrows(4)) dotmatrix_1 (
    .row0(tttc_1_l0), .row1(tttc_1_l1), .row2(tttc_1_l2), .row3(tttc_1_l3));
  TTTC tttc_1 (
    .hin(lll1_1_v2), .vin(lll1_1_h0), .btn(button_1_out), .L0(tttc_1_l0), .L1(tttc_1_l1), .L2(tttc_1_l2),
    .L3(tttc_1_l3), .hout(tttc_1_hout[2]), .vout(tttc_1_vout[2]), .taken(_00));
  Button button_1 (.out(button_1_out));
  DotMatrix #(.inputtype("row"), .matrixcols(4), .matrixrows(4)) dotmatrix_2 (
    .row0(tttc_2_l0), .row1(tttc_2_l1), .row2(tttc_2_l2), .row3(tttc_2_l3));
  TTTC tttc_2 (
    .hin(lll1_1_v1), .vin(lll1_1_h0), .btn(button_2_out), .L0(tttc_2_l0), .L1(tttc_2_l1), .L2(tttc_2_l2),
    .L3(tttc_2_l3), .hout(tttc_2_hout[2]), .vout(tttc_1_vout[2]), .taken(_01));
  Button button_2 (.out(button_2_out));
  DotMatrix #(.inputtype("row"), .matrixcols(4), .matrixrows(4)) dotmatrix_3 (
    .row0(tttc_3_l0), .row1(tttc_3_l1), .row2(tttc_3_l2), .row3(tttc_3_l3));
  TTTC tttc_3 (
    .hin(lll1_1_v0), .vin(lll1_1_h0), .btn(button_3_out), .L0(tttc_3_l0), .L1(tttc_3_l1), .L2(tttc_3_l2),
    .L3(tttc_3_l3), .hout(tttc_3_hout[2]), .vout(tttc_1_vout[2]), .taken(_02));
  Button button_3 (.out(button_3_out));
  DotMatrix #(.inputtype("row"), .matrixcols(4), .matrixrows(4)) dotmatrix_4 (
    .row0(tttc_4_l0), .row1(tttc_4_l1), .row2(tttc_4_l2), .row3(tttc_4_l3));
  TTTC tttc_4 (
    .hin(lll1_1_v2), .vin(lll1_1_h1), .btn(button_6_out), .L0(tttc_4_l0), .L1(tttc_4_l1), .L2(tttc_4_l2),
    .L3(tttc_4_l3), .hout(tttc_1_hout[2]), .vout(tttc_4_vout[2]), .taken(_10));
  TTTC tttc_5 (
    .hin(lll1_1_v1), .vin(lll1_1_h1), .btn(button_4_out), .L0(tttc_5_l0), .L1(tttc_5_l1), .L2(tttc_5_l2),
    .L3(tttc_5_l3), .hout(tttc_2_hout[2]), .vout(tttc_4_vout[2]), .taken(_11));
  DotMatrix #(.inputtype("row"), .matrixcols(4), .matrixrows(4)) dotmatrix_5 (
    .row0(tttc_5_l0), .row1(tttc_5_l1), .row2(tttc_5_l2), .row3(tttc_5_l3));
  Button button_4 (.out(button_4_out));
  TTTC tttc_6 (
    .hin(lll1_1_v0), .vin(lll1_1_h1), .btn(button_5_out), .L0(tttc_6_l0), .L1(tttc_6_l1), .L2(tttc_6_l2),
    .L3(tttc_6_l3), .hout(tttc_3_hout[2]), .vout(tttc_4_vout[2]), .taken(_12));
  DotMatrix #(.inputtype("row"), .matrixcols(4), .matrixrows(4)) dotmatrix_6 (
    .row0(tttc_6_l0), .row1(tttc_6_l1), .row2(tttc_6_l2), .row3(tttc_6_l3));
  Button button_5 (.out(button_5_out));
  Button button_6 (.out(button_6_out));
  // Probe on _11
  DotMatrix #(.inputtype("row"), .matrixcols(4), .matrixrows(4)) dotmatrix_7 (
    .row0(tttc_7_l0), .row1(tttc_7_l1), .row2(tttc_7_l2), .row3(tttc_7_l3));
  TTTC tttc_7 (
    .hin(lll1_1_v2), .vin(lll1_1_h2), .btn(button_7_out), .L0(tttc_7_l0), .L1(tttc_7_l1), .L2(tttc_7_l2),
    .L3(tttc_7_l3), .hout(tttc_1_hout[2]), .vout(tttc_7_vout[2]), .taken(_20));
  Button button_7 (.out(button_7_out));
  TTTC tttc_8 (
    .hin(lll1_1_v1), .vin(lll1_1_h2), .btn(button_8_out), .L0(tttc_8_l0), .L1(tttc_8_l1), .L2(tttc_8_l2),
    .L3(tttc_8_l3), .hout(tttc_2_hout[2]), .vout(tttc_7_vout[2]), .taken(_21));
  DotMatrix #(.inputtype("row"), .matrixcols(4), .matrixrows(4)) dotmatrix_8 (
    .row0(tttc_8_l0), .row1(tttc_8_l1), .row2(tttc_8_l2), .row3(tttc_8_l3));
  Button button_8 (.out(button_8_out));
  TTTC tttc_9 (
    .hin(lll1_1_v0), .vin(lll1_1_h2), .btn(button_9_out), .L0(tttc_9_l0), .L1(tttc_9_l1), .L2(tttc_9_l2),
    .L3(tttc_9_l3), .hout(tttc_3_hout[2]), .vout(tttc_7_vout[2]), .taken(_22));
  DotMatrix #(.inputtype("row"), .matrixcols(4), .matrixrows(4)) dotmatrix_9 (
    .row0(tttc_9_l0), .row1(tttc_9_l1), .row2(tttc_9_l2), .row3(tttc_9_l3));
  Button button_9 (.out(button_9_out));
  // Probe on {bbb_1_xy[7], 1'b0, State, bbb_1_xy[3:0]}
  BBB bbb_1 (
    .H0(tttc_1_hout[2]), .H1(tttc_2_hout[2]), .H2(tttc_3_hout[2]), .XY(bbb_1_xy[3:0]), .ready(bbb_1_xy[7]),
    .V0(tttc_7_vout[2]), .V1(tttc_4_vout[2]), .V2(tttc_1_vout[2]), .reset(decoder_1_out1));  // open: ready_prime
  assign I_Odat = decoder_1_out1 ? {bbb_1_xy[7], 1'b0, State, bbb_1_xy[3:0]} : 8'bz;  // Controlled_Buffer controlled_buffer_1
  state state_1 (
    ._00(_00), ._10(_10), ._20(_20), ._01(_01), ._11(_11), ._21(_21), ._02(_02), ._12(_12), ._22(_22),
    .game_state(State));
  // Probe on cdm_8_mark5_1_p5
  Clock clock_1 (.out(Cl));
  // Probe on cdm_8_mark5_1_p4
  // Probe on cdm_8_mark5_1_p2
  // Probe on cdm_8_mark5_1_p6
  // Probe on cdm_8_mark5_1_p1
  // Probe on I_Oadr
  and and_1 (I_Osel, and_3_out, Cl, data);
  // Probe on cdm_8_mark5_1_p7
  // Probe on cdm_8_mark5_1_p8
  // CdM_8_mark5 cdm_8_mark5_1: pin names not known; wires that end beside it: cdm_8_mark5_1_p1, cdm_8_mark5_1_p2, Cl, cdm_8_mark5_1_p4, cdm_8_mark5_1_p5, cdm_8_mark5_1_p6, cdm_8_mark5_1_p7, cdm_8_mark5_1_p8, cdm_8_mark5_1_p9, mem, In_out_prime, {cdm_8_mark5_1_p12, I_Oadr}, cdm_8_mark5_1_p13, cdm_8_mark5_1_p14
  and and_2 (RAM, ~and_3_out, data);  // AND_Gate
  Comparator #(.width(4), .mode("unsigned")) comparator_1 (
    .a(4'b0011), .b(I_Oadr), .gt(comparator_1_gt));  // open: eq, lt
  // Probe on {cdm_8_mark5_1_p12, I_Oadr}
  assign I_Odat = not_1_out ? cdm_8_mark5_1_p13 : 8'bz;  // Controlled_Buffer controlled_buffer_2
  not not_1 (not_1_out, In_out_prime);
  assign cdm_8_mark5_1_p14 = In_out_prime ? I_Odat : 8'bz;  // Controlled_Buffer controlled_buffer_3
  and and_3 (and_3_out, comparator_1_gt, comparator_2_eq);
  Comparator #(.width(4)) comparator_2 (.a(4'b1111), .b(cdm_8_mark5_1_p12), .eq(comparator_2_eq));  // open: gt, lt
  and IO_3_2 (IO_3_2_out, I_Osel, ~I_Oadr[0], I_Oadr[1], ~I_Oadr[2], ~I_Oadr[3]);  // AND_Gate
  and IO_3_3 (IO_3_3_out, I_Osel, I_Oadr[0], ~I_Oadr[1], ~I_Oadr[2], ~I_Oadr[3]);  // AND_Gate
  Decoder #(.disabled(0)) decoder_2 (.out0(code), .out1(data), .sel(cdm_8_mark5_1_p9), .en(mem));
  and and_4 (and_4_out, In_out_prime, IO_3_2_out);
  and and_5 (and_5_out, In_out_prime, IO_3_3_out);
  comp_turn comp_turn_1 (
    ._00(_00), ._10(_10), ._20(_20), ._01(_01), ._11(_11), ._21(_21), ._02(_02), ._12(_12), ._22(_22),
    .nought_coord(comp_turn_1_nought_coord));
  assign I_Odat = and_4_out ? {{6{1'b0}}, State} : 8'bz;  // Controlled_Buffer controlled_buffer_4
  // Probe on {{6{1'b0}}, State}
  assign I_Odat = and_5_out ? comp_turn_1_nought_coord : 8'bz;  // Controlled_Buffer controlled_buffer_5
  // Probe on comp_turn_1_nought_coord
  Pull_Resistor pull_resistor_1 (.node(I_Oadr[0]));
  Pull_Resistor pull_resistor_2 (.node(I_Oadr[1]));
  Pull_Resistor pull_resistor_3 (.node(I_Oadr[2]));
  Pull_Resistor pull_resistor_4 (.node(I_Oadr[3]));
  Pull_Resistor pull_resistor_5 (.node(cdm_8_mark5_1_p12[0]));
  Pull_Resistor pull_resistor_6 (.node(cdm_8_mark5_1_p12[1]));
  Pull_Resistor pull_resistor_7 (.node(cdm_8_mark5_1_p12[2]));
  Pull_Resistor pull_resistor_8 (.node(cdm_8_mark5_1_p12[3]));
  ROM rom_1 (.addr({cdm_8_mark5_1_p12, I_Oadr}), .data(I_Odat), .sel(code));
  RAM ram_1 (.addr({cdm_8_mark5_1_p12, I_Oadr}), .data(I_Odat), .sel(RAM), .clk(Cl), .ld(In_out_prime), .clr(rst));

  // Other names for the same wires on the sheet: rd_wr_prime = In_out_prime

  // Notes on the sheet:
  //   contents of rom_1 (hex, n*v repeats v):
  //   d0 f0 b1 5 e5 2 d2 3 46 c2 d2 c 46 9a 9a c2 d3 1 c5 95 95 57 c5 4*95 57 a3 d6 2b 0 e1 2f d6 39 d6 2b
  //   0 e1 2f ee 0 d0 f2 b0 d7 d1 3c 90 90 90 54 d1 f0 a4 d4 d0 f1 b0 94 94 d1 2 54 d1 f0 a4 d7 171*0 80
endmodule

module BBB (
  input  H0,
  input  H1,
  input  H2,
  input  reset,
  input  V0,
  input  V1,
  input  V2,
  output [3:0] XY,
  output ready,
  output ready_prime
);

  wire b_press_out, btn, nand_1_out, nand_2_out, not_1_out, not_2_out, rst;
  wire [1:0] transistor_1_out, transistor_4_out;

  Pull_Resistor #(.pull(1)) pull_resistor_1 (.node(V1));
  Pull_Resistor #(.pull(1)) pull_resistor_2 (.node(V2));
  Pull_Resistor #(.pull(1)) pull_resistor_3 (.node(V0));
  Pull_Resistor #(.pull(1)) pull_resistor_4 (.node(H0));
  Pull_Resistor #(.pull(1)) pull_resistor_5 (.node(H2));
  Pull_Resistor #(.pull(1)) pull_resistor_6 (.node(H1));
  Transistor #(.gate("br"), .width(2)) transistor_1 (.in(2'b00), .out(transistor_1_out), .gate(V2));
  Transistor #(.gate("br"), .width(2)) transistor_2 (.in(2'b01), .out(transistor_1_out), .gate(V1));
  Transistor #(.gate("br"), .width(2)) transistor_3 (.in(2'b10), .out(transistor_1_out), .gate(V0));
  Transistor #(.width(2)) transistor_4 (.in(2'b00), .out(transistor_4_out), .gate(H0));
  Transistor #(.width(2)) transistor_5 (.in(2'b01), .out(transistor_4_out), .gate(H1));
  nand nand_1 (nand_1_out, H0, H1, H2);
  nand nand_2 (nand_2_out, V2, V1, V0);
  Transistor #(.width(2)) transistor_6 (.in(2'b10), .out(transistor_4_out), .gate(H2));
  and b_press (b_press_out, nand_1_out, nand_2_out);
  not not_1 (not_1_out, reset);
  not not_2 (not_2_out, b_press_out);
  Register #(.width(4)) XY_reg (.D({transistor_1_out, transistor_4_out}), .Q(XY), .clk(b_press_out));  // open: en, clr
  and u_btn (btn, not_2_out, b_press_out);
  nor u_rst (rst, not_1_out, reset);
  S_R_Flip_Flop #(.trigger("high")) s_r_ff_1 (
    .S(btn), .clk(1'b1), .R(rst), .Q(ready), .Qn(ready_prime));  // open: preset, reset, en
endmodule

// Tic Tac Toe
module TTTC (
  input  [1:0] hin,
  input  [1:0] vin,
  input  btn,
  output [1:0] taken,
  output [3:0] L0,
  output [3:0] L1,
  output [3:0] L2,
  output [3:0] L3,
  output hout,
  output vout
);

  wire and_1_out, and_2_out, nor_1_out;

  and and_1 (and_1_out, hin[1], vin[1]);
  // Probe on and_1_out
  // Probe on {hin[0], vin[0]}
  // Probe on taken
  Register #(.width(2)) register_1 (.D({hin[0], vin[0]}), .en(and_1_out), .Q(taken), .clk(and_1_out), .clr(1'b0));
  nor nor_1 (nor_1_out, taken[0], taken[1]);
  and and_2 (and_2_out, nor_1_out, btn);
  ROM #(.addrWidth(2), .dataWidth(16)) rom_1 (.addr(taken), .data({L3, L2, L1, L0}));  // open: sel
  Transistor #(.\type ("n")) transistor_1 (.in(1'b0), .out(hout), .gate(and_2_out));

  assign vout = hout;

  // Notes on the sheet:
  //   contents of rom_1 (hex, n*v repeats v):
  //   0 9429 f99f
endmodule

module rsfp (
  input  S,
  input  R,
  output Q,
  output Q_prime
);
endmodule

module I_Win (
  input  [1:0] score,
  input  clock,
  output lose,
  output win,
  output draw
);

  wire [1:0] register_1_q;

  Register #(.width(2)) register_1 (.D(score), .en(clock), .Q(register_1_q), .clk(clock));  // open: clr
  and and_1 (lose, ~register_1_q[0], register_1_q[1]);  // AND_Gate
  and and_2 (win, register_1_q[0], ~register_1_q[1]);  // AND_Gate
  and and_3 (draw, register_1_q[0], register_1_q[1]);
endmodule

module LLL1 (
  input  [1:0] symID,
  input  [3:0] XY,
  input  clock,
  output [1:0] V0,
  output [1:0] V1,
  output [1:0] V2,
  output [1:0] H0,
  output [1:0] H1,
  output [1:0] H2
);

  wire and_1_out, and_2_out, and_3_out, and_4_out, and_5_out, and_6_out;

  Pull_Resistor #(.pull(1)) pull_resistor_1 (.node(XY));
  // Probe on XY[1:0]
  and and_1 (and_1_out, ~XY[2], XY[3]);  // AND_Gate
  and and_2 (and_2_out, XY[2], ~XY[3]);  // AND_Gate
  and and_3 (and_3_out, ~XY[2], ~XY[3]);  // AND_Gate
  and and_4 (and_4_out, ~XY[0], ~XY[1]);  // AND_Gate
  and and_5 (and_5_out, XY[0], ~XY[1]);  // AND_Gate
  and and_6 (and_6_out, ~XY[0], XY[1]);  // AND_Gate
  assign H0 = and_4_out ? {clock, symID[0]} : 2'bz;  // Controlled_Buffer controlled_buffer_1
  assign V0 = and_1_out ? {clock, symID[1]} : 2'bz;  // Controlled_Buffer controlled_buffer_2
  assign V1 = and_2_out ? {clock, symID[1]} : 2'bz;  // Controlled_Buffer controlled_buffer_3
  assign V2 = and_3_out ? {clock, symID[1]} : 2'bz;  // Controlled_Buffer controlled_buffer_4
  assign H1 = and_5_out ? {clock, symID[0]} : 2'bz;  // Controlled_Buffer controlled_buffer_5
  assign H2 = and_6_out ? {clock, symID[0]} : 2'bz;  // Controlled_Buffer controlled_buffer_6

  // Notes on the sheet:
  //   clock: pull=down
endmodule

module state (
  input  [1:0] _00,
  input  [1:0] _10,
  input  [1:0] _20,
  input  [1:0] _01,
  input  [1:0] _11,
  input  [1:0] _21,
  input  [1:0] _02,
  input  [1:0] _12,
  input  [1:0] _22,
  output [1:0] game_state
);

  wire draw_prime_out, nor_1_out, nor_2_out, nor_3_out, nor_4_out, nor_5_out, nor_6_out, nor_7_out,
       nor_8_out, nor_9_out, or_2_out;
  wire [1:0] n3cell_check_1_game_state, n3cell_check_2_game_state, n3cell_check_3_game_state,
       n3cell_check_4_game_state, n3cell_check_5_game_state, n3cell_check_6_game_state,
       n3cell_check_7_game_state, n3cell_check_8_game_state, or_1_out;

  _3cell_check u_3cell_check_1 (.in_1(_00), .in_2(_01), .in_3(_02), .game_state(n3cell_check_1_game_state));
  _3cell_check u_3cell_check_2 (.in_1(_10), .in_2(_11), .in_3(_12), .game_state(n3cell_check_2_game_state));
  _3cell_check u_3cell_check_3 (.in_1(_20), .in_2(_21), .in_3(_22), .game_state(n3cell_check_3_game_state));
  nor nor_1 (nor_1_out, _00[0], _00[1]);
  nor nor_2 (nor_2_out, _10[0], _10[1]);
  nor nor_3 (nor_3_out, _20[0], _20[1]);
  nor nor_4 (nor_4_out, _01[0], _01[1]);
  nor nor_5 (nor_5_out, _11[0], _11[1]);
  nor nor_6 (nor_6_out, _21[0], _21[1]);
  nor nor_7 (nor_7_out, _02[0], _02[1]);
  nor nor_8 (nor_8_out, _12[0], _12[1]);
  nor nor_9 (nor_9_out, _22[0], _22[1]);
  _3cell_check u_3cell_check_4 (.in_1(_00), .in_2(_10), .in_3(_20), .game_state(n3cell_check_4_game_state));
  _3cell_check u_3cell_check_5 (.in_1(_01), .in_2(_11), .in_3(_21), .game_state(n3cell_check_5_game_state));
  _3cell_check u_3cell_check_6 (.in_1(_02), .in_2(_12), .in_3(_22), .game_state(n3cell_check_6_game_state));
  _3cell_check u_3cell_check_7 (.in_1(_00), .in_2(_11), .in_3(_22), .game_state(n3cell_check_7_game_state));
  _3cell_check u_3cell_check_8 (.in_1(_20), .in_2(_11), .in_3(_02), .game_state(n3cell_check_8_game_state));
  or draw_prime (draw_prime_out, nor_1_out, nor_2_out, nor_3_out, nor_4_out, nor_8_out, nor_5_out, nor_6_out, nor_7_out, nor_9_out);
  assign or_1_out = n3cell_check_1_game_state | n3cell_check_2_game_state | n3cell_check_3_game_state | n3cell_check_4_game_state | n3cell_check_5_game_state | n3cell_check_6_game_state | n3cell_check_7_game_state | n3cell_check_8_game_state;  // OR_Gate or_1, 2 bits wide
  Multiplexer #(.width(2), .enable("false")) multiplexer_1 (
    .in0(2'b11), .in1(or_1_out), .out(game_state), .sel(or_2_out));
  or or_2 (or_2_out, draw_prime_out, or_1_out[0], or_1_out[1]);
endmodule

// 3cell
module _3cell_check (
  input  [1:0] in_1,
  input  [1:0] in_2,
  input  [1:0] in_3,
  output [1:0] game_state
);

  wire and_1_out, comparator_1_eq, comparator_2_eq;

  Comparator #(.width(2)) comparator_1 (.a(in_1), .b(in_2), .eq(comparator_1_eq));  // open: gt, lt
  Comparator #(.width(2)) comparator_2 (.a(in_2), .b(in_3), .eq(comparator_2_eq));  // open: gt, lt
  and and_1 (and_1_out, comparator_1_eq, comparator_2_eq);
  Multiplexer #(.width(2), .enable("false")) multiplexer_1 (.in0(2'b00), .in1(in_1), .out(game_state), .sel(and_1_out));
endmodule

// CT
module comp_turn (
  input  [1:0] _00,
  input  [1:0] _10,
  input  [1:0] _20,
  input  [1:0] _01,
  input  [1:0] _11,
  input  [1:0] _21,
  input  [1:0] _02,
  input  [1:0] _12,
  input  [1:0] _22,
  output [7:0] nought_coord
);

  wire comparator_1_lt, comparator_2_lt, comparator_3_lt, comparator_4_lt, comparator_5_lt, comparator_6_lt,
       comparator_7_lt, comparator_8_lt, nor_1_out, nor_2_out, nor_3_out, nor_4_out, nor_5_out, nor_6_out,
       nor_7_out, nor_8_out, nor_9_out;
  wire [5:0] counter_1_summ_help, counter_2_summ_help, counter_3_summ_help, counter_4_summ_help,
       counter_5_summ_help, counter_6_summ_help, counter_7_summ_help, counter_8_summ_help,
       counter_9_summ_help, multiplexer_8_out;
  wire [9:0] multiplexer_1_out, multiplexer_2_out, multiplexer_3_out, multiplexer_4_out, multiplexer_5_out,
       multiplexer_6_out, multiplexer_7_out;

  nor nor_1 (nor_1_out, _00[0], _00[1]);
  nor nor_2 (nor_2_out, _10[0], _10[1]);
  nor nor_3 (nor_3_out, _20[0], _20[1]);
  nor nor_4 (nor_4_out, _01[0], _01[1]);
  nor nor_5 (nor_5_out, _11[0], _11[1]);
  nor nor_6 (nor_6_out, _21[0], _21[1]);
  nor nor_7 (nor_7_out, _02[0], _02[1]);
  nor nor_8 (nor_8_out, _12[0], _12[1]);
  nor nor_9 (nor_9_out, _22[0], _22[1]);
  // Probe on counter_1_summ_help
  counter counter_1 (
    ._00(_00), ._10(_10), ._20(_20), ._01(_01), ._11(_11), ._21(_21), ._02(_02), ._12(_12), ._22(_22),
    .in_10(nor_1_out), .in_11(4'b0000), .summ_help(counter_1_summ_help));
  // Probe on counter_2_summ_help
  counter counter_2 (
    ._00(_00), ._10(_10), ._20(_20), ._01(_01), ._11(_11), ._21(_21), ._02(_02), ._12(_12), ._22(_22),
    .in_10(nor_2_out), .in_11(4'b0100), .summ_help(counter_2_summ_help));
  // Probe on counter_3_summ_help
  counter counter_3 (
    ._00(_00), ._10(_10), ._20(_20), ._01(_01), ._11(_11), ._21(_21), ._02(_02), ._12(_12), ._22(_22),
    .in_10(nor_3_out), .in_11(4'b1000), .summ_help(counter_3_summ_help));
  // Probe on counter_4_summ_help
  counter counter_4 (
    ._00(_00), ._10(_10), ._20(_20), ._01(_01), ._11(_11), ._21(_21), ._02(_02), ._12(_12), ._22(_22),
    .in_10(nor_4_out), .in_11(4'b0001), .summ_help(counter_4_summ_help));
  // Probe on counter_5_summ_help
  counter counter_5 (
    ._00(_00), ._10(_10), ._20(_20), ._01(_01), ._11(_11), ._21(_21), ._02(_02), ._12(_12), ._22(_22),
    .in_10(nor_5_out), .in_11(4'b0101), .summ_help(counter_5_summ_help));
  // Probe on counter_6_summ_help
  counter counter_6 (
    ._00(_00), ._10(_10), ._20(_20), ._01(_01), ._11(_11), ._21(_21), ._02(_02), ._12(_12), ._22(_22),
    .in_10(nor_6_out), .in_11(4'b1001), .summ_help(counter_6_summ_help));
  // Probe on counter_7_summ_help
  counter counter_7 (
    ._00(_00), ._10(_10), ._20(_20), ._01(_01), ._11(_11), ._21(_21), ._02(_02), ._12(_12), ._22(_22),
    .in_10(nor_7_out), .in_11(4'b0010), .summ_help(counter_7_summ_help));
  // Probe on counter_8_summ_help
  counter counter_8 (
    ._00(_00), ._10(_10), ._20(_20), ._01(_01), ._11(_11), ._21(_21), ._02(_02), ._12(_12), ._22(_22),
    .in_10(nor_8_out), .in_11(4'b0110), .summ_help(counter_8_summ_help));
  // Probe on counter_9_summ_help
  counter counter_9 (
    ._00(_00), ._10(_10), ._20(_20), ._01(_01), ._11(_11), ._21(_21), ._02(_02), ._12(_12), ._22(_22),
    .in_10(nor_9_out), .in_11(4'b1010), .summ_help(counter_9_summ_help));
  Comparator #(.width(6), .mode("unsigned")) comparator_1 (
    .a(counter_1_summ_help), .b(counter_2_summ_help), .lt(comparator_1_lt));  // open: gt, eq
  Multiplexer #(.width(10), .enable("false")) multiplexer_1 (
    .in0({4'b0000, counter_1_summ_help}), .in1({4'b0100, counter_2_summ_help}), .out(multiplexer_1_out),
    .sel(comparator_1_lt));
  Comparator #(.width(6), .mode("unsigned")) comparator_2 (
    .a(multiplexer_1_out[5:0]), .b(counter_3_summ_help), .lt(comparator_2_lt));  // open: gt, eq
  Comparator #(.width(6), .mode("unsigned")) comparator_3 (
    .a(multiplexer_2_out[5:0]), .b(counter_4_summ_help), .lt(comparator_3_lt));  // open: gt, eq
  Comparator #(.width(6), .mode("unsigned")) comparator_4 (
    .a(multiplexer_3_out[5:0]), .b(counter_5_summ_help), .lt(comparator_4_lt));  // open: gt, eq
  Comparator #(.width(6), .mode("unsigned")) comparator_5 (
    .a(multiplexer_4_out[5:0]), .b(counter_6_summ_help), .lt(comparator_5_lt));  // open: gt, eq
  Comparator #(.width(6), .mode("unsigned")) comparator_6 (
    .a(multiplexer_5_out[5:0]), .b(counter_7_summ_help), .lt(comparator_6_lt));  // open: gt, eq
  Comparator #(.width(6), .mode("unsigned")) comparator_7 (
    .a(multiplexer_6_out[5:0]), .b(counter_8_summ_help), .lt(comparator_7_lt));  // open: gt, eq
  Comparator #(.width(6), .mode("unsigned")) comparator_8 (
    .a(multiplexer_7_out[5:0]), .b(counter_9_summ_help), .lt(comparator_8_lt));  // open: gt, eq
  Multiplexer #(.width(10), .enable("false")) multiplexer_2 (
    .in0(multiplexer_1_out), .in1({4'b1000, counter_3_summ_help}), .out(multiplexer_2_out),
    .sel(comparator_2_lt));
  Multiplexer #(.width(10), .enable("false")) multiplexer_3 (
    .in0(multiplexer_2_out), .in1({4'b0001, counter_4_summ_help}), .out(multiplexer_3_out),
    .sel(comparator_3_lt));
  Multiplexer #(.width(10), .enable("false")) multiplexer_4 (
    .in0(multiplexer_3_out), .in1({4'b0101, counter_5_summ_help}), .out(multiplexer_4_out),
    .sel(comparator_4_lt));
  Multiplexer #(.width(10), .enable("false")) multiplexer_5 (
    .in0(multiplexer_4_out), .in1({4'b1001, counter_6_summ_help}), .out(multiplexer_5_out),
    .sel(comparator_5_lt));
  Multiplexer #(.width(10), .enable("false")) multiplexer_6 (
    .in0(multiplexer_5_out), .in1({4'b0010, counter_7_summ_help}), .out(multiplexer_6_out),
    .sel(comparator_6_lt));
  Multiplexer #(.width(10), .enable("false")) multiplexer_7 (
    .in0(multiplexer_6_out), .in1({4'b0110, counter_8_summ_help}), .out(multiplexer_7_out),
    .sel(comparator_7_lt));
  Multiplexer #(.width(10), .enable("false")) multiplexer_8 (
    .in0(multiplexer_7_out), .in1({4'b1010, counter_9_summ_help}),
    .out({nought_coord[1:0], nought_coord[3:2], multiplexer_8_out}), .sel(comparator_8_lt));

  assign nought_coord[7:4] = 4'b0000;
endmodule

module counter (
  input  [1:0] _00,
  input  [1:0] _10,
  input  [1:0] _20,
  input  [1:0] _01,
  input  [1:0] _11,
  input  [1:0] _21,
  input  [1:0] _02,
  input  [1:0] _12,
  input  [1:0] _22,
  input  in_10,
  input  [3:0] in_11,
  output [5:0] summ_help
);

  wire comparator_1_eq, comparator_2_eq, comparator_3_eq, comparator_4_eq, decoder_1_out0, decoder_1_out1,
       decoder_1_out2, decoder_2_out0, decoder_2_out1, decoder_2_out2, decoder_3_out0, decoder_3_out1,
       decoder_3_out2, decoder_4_out0, decoder_4_out1, decoder_4_out2;
  wire [1:0] adder_1_out, adder_2_out;
  wire [4:0] adder_3_out, adder_4_out, adder_5_out, adder_6_out, adder_7_out, adder_8_out, adder_9_out,
       adder_10_out, adder_11_out, adder_13_out, adder_14_out, adder_15_out, adder_16_out, adder_17_out,
       count_crosses_1_help, count_crosses_2_help, count_crosses_3_help, count_crosses_4_help,
       count_crosses_5_help, count_crosses_6_help, count_crosses_7_help, count_crosses_8_help,
       count_noughts_1_help, count_noughts_2_help, count_noughts_3_help, count_noughts_4_help,
       count_noughts_5_help, count_noughts_6_help, count_noughts_7_help, count_noughts_8_help;

  Decoder #(.select(2), .disabled(0)) decoder_1 (
    .out0(decoder_1_out0), .out1(decoder_1_out1), .out2(decoder_1_out2), .sel(in_11[3:2]), .en(in_10));  // open: out3
  Decoder #(.select(2), .disabled(0)) decoder_2 (
    .out0(decoder_2_out0), .out1(decoder_2_out1), .out2(decoder_2_out2), .sel(in_11[3:2]), .en(in_10));  // open: out3
  Decoder #(.select(2), .disabled(0)) decoder_3 (
    .out0(decoder_3_out0), .out1(decoder_3_out1), .out2(decoder_3_out2), .sel(in_11[1:0]), .en(in_10));  // open: out3
  Comparator #(.width(2)) comparator_1 (.a(in_11[1:0]), .b(in_11[3:2]), .eq(comparator_1_eq));  // open: gt, lt
  Adder #(.width(2)) adder_1 (.a(in_11[1:0]), .b(in_11[3:2]), .out(adder_1_out));  // open: cin, cout
  Decoder #(.select(2), .disabled(0)) decoder_4 (
    .out0(decoder_4_out0), .out1(decoder_4_out1), .out2(decoder_4_out2), .sel(in_11[1:0]), .en(in_10));  // open: out3
  Comparator #(.width(2)) comparator_2 (.a(in_11[1:0]), .b(in_11[3:2]), .eq(comparator_2_eq));  // open: gt, lt
  Adder #(.width(2)) adder_2 (.a(in_11[1:0]), .b(in_11[3:2]), .out(adder_2_out));  // open: cin, cout
  Comparator #(.width(2), .mode("unsigned")) comparator_3 (
    .a(adder_1_out), .b(2'b10), .eq(comparator_3_eq));  // open: gt, lt
  Comparator #(.width(2), .mode("unsigned")) comparator_4 (
    .a(adder_2_out), .b(2'b10), .eq(comparator_4_eq));  // open: gt, lt
  count_noughts count_noughts_1 (
    .in_1(_00), .in_2(_10), .in_3(_20), .in_4(decoder_3_out0), .help(count_noughts_1_help));
  count_noughts count_noughts_2 (
    .in_1(_00), .in_2(_01), .in_3(_02), .in_4(decoder_1_out0), .help(count_noughts_2_help));
  count_noughts count_noughts_3 (
    .in_1(_01), .in_2(_11), .in_3(_21), .in_4(decoder_3_out1), .help(count_noughts_3_help));
  count_noughts count_noughts_4 (
    .in_1(_10), .in_2(_11), .in_3(_12), .in_4(decoder_1_out1), .help(count_noughts_4_help));
  count_noughts count_noughts_5 (
    .in_1(_02), .in_2(_12), .in_3(_22), .in_4(decoder_3_out2), .help(count_noughts_5_help));
  count_noughts count_noughts_6 (
    .in_1(_20), .in_2(_21), .in_3(_22), .in_4(decoder_1_out2), .help(count_noughts_6_help));
  count_noughts count_noughts_7 (
    .in_1(_00), .in_2(_11), .in_3(_22), .in_4(comparator_1_eq), .help(count_noughts_7_help));
  count_noughts count_noughts_8 (
    .in_1(_20), .in_2(_11), .in_3(_02), .in_4(comparator_3_eq), .help(count_noughts_8_help));
  count_crosses count_crosses_1 (
    .in_1(_00), .in_2(_10), .in_3(_20), .in_4(decoder_4_out0), .help(count_crosses_1_help));
  count_crosses count_crosses_2 (
    .in_1(_00), .in_2(_01), .in_3(_02), .in_4(decoder_2_out0), .help(count_crosses_2_help));
  count_crosses count_crosses_3 (
    .in_1(_01), .in_2(_11), .in_3(_21), .in_4(decoder_4_out1), .help(count_crosses_3_help));
  count_crosses count_crosses_4 (
    .in_1(_10), .in_2(_11), .in_3(_12), .in_4(decoder_2_out1), .help(count_crosses_4_help));
  count_crosses count_crosses_5 (
    .in_1(_02), .in_2(_12), .in_3(_22), .in_4(decoder_4_out2), .help(count_crosses_5_help));
  count_crosses count_crosses_6 (
    .in_1(_20), .in_2(_21), .in_3(_22), .in_4(decoder_2_out2), .help(count_crosses_6_help));
  count_crosses count_crosses_7 (
    .in_1(_00), .in_2(_11), .in_3(_22), .in_4(comparator_2_eq), .help(count_crosses_7_help));
  count_crosses count_crosses_8 (
    .in_1(_20), .in_2(_11), .in_3(_02), .in_4(comparator_4_eq), .help(count_crosses_8_help));
  // Probe on count_crosses_1_help
  // Probe on count_crosses_2_help
  // Probe on count_crosses_3_help
  // Probe on count_crosses_4_help
  // Probe on count_crosses_6_help
  // Probe on count_crosses_7_help
  // Probe on count_crosses_8_help
  Adder #(.width(5)) adder_3 (
    .a(count_noughts_1_help), .b(count_noughts_2_help), .out(adder_3_out));  // open: cin, cout
  // Probe on count_noughts_4_help
  Adder #(.width(5)) adder_4 (
    .a(count_crosses_1_help), .b(count_crosses_2_help), .out(adder_4_out));  // open: cin, cout
  Adder #(.width(5)) adder_5 (.a(adder_3_out), .b(count_noughts_3_help), .out(adder_5_out));  // open: cin, cout
  Adder #(.width(5)) adder_6 (.a(adder_4_out), .b(count_crosses_3_help), .out(adder_6_out));  // open: cin, cout
  Adder #(.width(5)) adder_7 (.a(adder_5_out), .b(count_noughts_4_help), .out(adder_7_out));  // open: cin, cout
  Adder #(.width(5)) adder_8 (.a(adder_6_out), .b(count_crosses_4_help), .out(adder_8_out));  // open: cin, cout
  Adder #(.width(5)) adder_9 (.a(adder_7_out), .b(count_noughts_5_help), .out(adder_9_out));  // open: cin, cout
  Adder #(.width(5)) adder_10 (.a(adder_8_out), .b(count_crosses_5_help), .out(adder_10_out));  // open: cin, cout
  Adder #(.width(5)) adder_11 (.a(adder_9_out), .b(count_noughts_6_help), .out(adder_11_out));  // open: cin, cout
  Adder #(.width(6)) adder_12 (.a({1'b0, adder_15_out}), .b({1'b0, adder_17_out}), .out(summ_help));  // open: cin, cout
  // Probe on adder_17_out
  Adder #(.width(5)) adder_13 (.a(adder_10_out), .b(count_crosses_6_help), .out(adder_13_out));  // open: cin, cout
  Adder #(.width(5)) adder_14 (.a(adder_11_out), .b(count_noughts_7_help), .out(adder_14_out));  // open: cin, cout
  Adder #(.width(5)) adder_15 (.a(adder_14_out), .b(count_noughts_8_help), .out(adder_15_out));  // open: cin, cout
  Adder #(.width(5)) adder_16 (.a(adder_13_out), .b(count_crosses_7_help), .out(adder_16_out));  // open: cin, cout
  Adder #(.width(5)) adder_17 (.a(adder_16_out), .b(count_crosses_8_help), .out(adder_17_out));  // open: cin, cout
endmodule

module count_noughts (
  input  [1:0] in_1,
  input  [1:0] in_2,
  input  [1:0] in_3,
  input  in_4,
  output [4:0] help
);

  wire or_1_out;
  wire [2:0] bitadder_1_out;

  or or_1 (or_1_out, ~in_4, in_1[0], in_2[0], in_3[0]);  // OR_Gate
  BitAdder #(.width(1)) bitadder_1 (.in0(in_1[1]), .in1(in_2[1]), .in2(in_3[1]), .in3(in_4), .out(bitadder_1_out));
  Multiplexer #(.width(3), .enable("false")) multiplexer_1 (
    .in0(bitadder_1_out), .in1(3'b000), .out(help[2:0]), .sel(or_1_out));

  assign help[4:3] = 2'b00;
endmodule

module count_crosses (
  input  [1:0] in_1,
  input  [1:0] in_2,
  input  [1:0] in_3,
  input  in_4,
  output [4:0] help
);

  wire and_1_out, or_1_out;
  wire [2:0] bitadder_1_out, multiplexer_1_out;

  or or_1 (or_1_out, ~in_4, in_1[1], in_3[1], in_2[1]);  // OR_Gate
  BitAdder #(.width(1)) bitadder_1 (.in0(in_1[0]), .in1(in_2[0]), .in2(in_3[0]), .in3(in_4), .out(bitadder_1_out));
  Multiplexer #(.width(3), .enable("false")) multiplexer_1 (
    .in0(bitadder_1_out), .in1(3'b000), .out(multiplexer_1_out), .sel(or_1_out));
  and and_1 (and_1_out, multiplexer_1_out[0], multiplexer_1_out[1], ~multiplexer_1_out[2]);  // AND_Gate
  Multiplexer #(.width(3), .enable("false")) multiplexer_2 (
    .in0(multiplexer_1_out), .in1(3'b110), .out(help[2:0]), .sel(and_1_out));

  assign help[4:3] = 2'b00;
endmodule
